# Fritzing sketch Porsche_Automatik_Bedienteil (saved by Fritzing 0.9.2b)
breadboards: 1

parts:
  U6 = mystery part, 6 pins [chip_label="4 Channel Relay"]
  U7 = mystery part, 3 pins [chip_label=Relay]
  U5 = POT [package=pot_alpha_rv16af-20]
  S2 = Round Pushbutton
  S1 = Round Pushbutton
  U2 = MCP42xxx [package=so014]
  Bauteil1 = Arduino Uno (Rev3)
  U1 = MCP42xxx [package=so014]
  LCD1 = LCD screen
  LCM1602_IIC1 = LCM1602 IIC [part_number="LCM1602 IIC" chip_label="LCM1602 IIC" package="DIP (Dual Inline) [THT]"]
  JP1 = Header 3 [package=molex-1x3_lock]
  JP2 = Header 3 [package=molex-1x3_lock]
  JP3 = Header 3 [package=molex-1x3_lock]
  JP4 = Header 3 [package=molex-1x3_lock]

nets:
  GND: U6.pin1, U7.pin2, U5.A, S2.leg1, S1.leg1, U2.GND, Bauteil1.GND, U1.GND, LCM1602_IIC1.GND
  N1: U6.pin2, Bauteil1.D4
  N2: U6.pin3, Bauteil1.D5_PWM
  N3: U6.pin4, Bauteil1.D6_PWM
  N4: U6.pin5, Bauteil1.D7
  VCC: U6.pin6, U7.pin1, U5.E, U2.RST, U2.SHTDWN, U2.DO, U2.VCC, Bauteil1.5V, U1.RST, U1.SHTDWN, U1.DO, U1.VCC, LCM1602_IIC1.VCC
  N5: U7.pin3, Bauteil1.D8
  N6: U5.S, Bauteil1.A1
  N7: S2.leg0, Bauteil1.D3_PWM
  N8: S1.leg0, Bauteil1.D2
  N9: U2.CS, Bauteil1.D9_PWM
  N10: U2.SCK, Bauteil1.D13/SCK, U1.SCK
  N11: U2.DI, Bauteil1.D11_PWM/MOSI, U1.DI
  N12: U2.B1, JP4.1
  N13: U2.W1, JP4.2
  N14: U2.A1, JP4.3
  N15: U2.A0, JP3.3
  N16: U2.W0, JP3.2
  N17: U2.B0, JP3.1
  N18: Bauteil1.A4/SDA, LCM1602_IIC1.SDA
  N19: Bauteil1.A5/SCL, LCM1602_IIC1.SCL
  N20: Bauteil1.D10_PWM/SS, U1.CS
  N21: U1.B1, JP1.1
  N22: U1.W1, JP1.2
  N23: U1.A1, JP1.3
  N24: U1.A0, JP2.3
  N25: U1.W0, JP2.2
  N26: U1.B0, JP2.1
  VSS: LCD1.VSS, LCM1602_IIC1.VSS
  VDD: LCD1.VDD, LCM1602_IIC1.VDD
  N27: LCD1.V0, LCM1602_IIC1.V0
  N28: LCD1.RS, LCM1602_IIC1.RS
  N29: LCD1.R/W, LCM1602_IIC1.RW
  N30: LCD1.E, LCM1602_IIC1.E
  N31: LCD1.DB0, LCM1602_IIC1.D0
  N32: LCD1.DB1, LCM1602_IIC1.D1
  N33: LCD1.DB2, LCM1602_IIC1.D2
  N34: LCD1.DB3, LCM1602_IIC1.D3
  N35: LCD1.DB4, LCM1602_IIC1.D4
  N36: LCD1.DB5, LCM1602_IIC1.D5
  N37: LCD1.DB6, LCM1602_IIC1.D6
  N38: LCD1.DB7, LCM1602_IIC1.D7
  N39: LCD1.LED+, LCM1602_IIC1.A
  N40: LCD1.LED-, LCM1602_IIC1.K
  N41: LCM1602_IIC1.LED_A, LCM1602_IIC1.LED_B

custom parts:
  LCM1602 IIC: I2C-Module to use a 1602 or 2004 LCD on with the wire.h libory Serial LCD Modul
